# Fritzing sketch board (saved by Fritzing 0.9.10b)
breadboards: 1

parts:
  M1 = ESP32-S2-DevKitC-1 [part_number=ESP32-S2-DevKitC-1]
  SD_card_module1 = SD Card Module
  Componente1 = PN532 Elechouse RFID NFC Module V3
  M2 = cc1101 module
  Componente2 = GMT020-02 TFT Display

nets:
  N1: M1.pin_1, M1.pin_2, SD_card_module1.+3.3, Componente1.VCC, M2.pin_1
  N2: M1.pin_4, Componente1.IRQ, Componente2.RST
  N3: M1.pin_5, Componente1.RSTO, Componente2.DC
  N4: M1.pin_12, Componente1.SDA
  N5: M1.pin_13, Componente1.SCL
  N6: M1.pin_16, SD_card_module1.CS, Componente2.CS
  N7: M1.pin_17, SD_card_module1.MOSI, M2.pin_3, Componente2.SDA(MOSI)
  N8: M1.pin_18, SD_card_module1.MISO, M2.pin_5, Componente2.SCL(SCLK)
  N9: M1.pin_19, SD_card_module1.SCK, M2.pin_4
  GND: M1.pin_22, M1.pin_23, M1.pin_24, M1.pin_44, SD_card_module1.GND, Componente1.GND, M2.pin_9
  N10: M1.pin_26, M2.pin_6
  N11: M1.pin_27, M2.pin_8
  N12: M1.pin_32, M2.pin_7

notes:
  PN532 in I2C mode
  to SPI pin
  CS: pin 14
  to SPI pin
  to SPI pin
  CS: pin 10

custom parts:
  ESP32-S2-DevKitC-1: ESP32-S2-DevKitC-1 is an entry-level development board based on ESP32-S2-SOLO (on-board PCB antenna). It is based on the ESP32 microcontroller that boasts Wifi, Bluetooth, Ethernet and Low Power support all in a single chip. (vanepp) Feb 2022: converted to ESP32-S2-DevKitC-1. This module is 44pins long (2x22) and 11 pins width.
  SD Card Module: SD Card Module Slot Socket Reader For Arduino ARM MCU
  PN532 Elechouse RFID NFC Module V3: NFC is a popular technology in recent years. We often heard this work while smart phone company such as Samsung or HTC introduces their latest high-end phones. Almost all the high-end phone in the market support NFC. Near field communication (NFC) is a set of standards for smart phones and similar devices to establish radio communication with each other by touching them together or bringing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
  cc1101 module: CC1101 rf module.
  GMT020-02 TFT Display: TFT Display 240x320 with ST7789 or compatible driver, SPI bus. This part is made from Adafruit ST7789 2.0 display.
